// Logisim project Nano8v1.circ as structural Verilog
module CPU (
);

  wire AI, AO, BI, BO, CI, CLK, CO, demultiplexer_1_out4, demultiplexer_1_out5, demultiplexer_1_out6,
       demultiplexer_1_out7, demultiplexer_1_out8, demultiplexer_1_out9, demultiplexer_1_out10,
       demultiplexer_1_out11, demultiplexer_1_out12, demultiplexer_1_out13, demultiplexer_1_out14,
       demultiplexer_1_out15, demultiplexer_2_out4, demultiplexer_2_out5, demultiplexer_2_out6,
       demultiplexer_2_out7, demultiplexer_2_out8, demultiplexer_2_out9, demultiplexer_2_out10,
       demultiplexer_2_out11, demultiplexer_2_out12, demultiplexer_2_out13, demultiplexer_2_out14,
       demultiplexer_2_out15, dipswitch_2_p1, MAN, RES;
  wire [3:0] CIN, COUT, undriven_2, undriven_3;
  wire [7:0] DATA, register_1_q, register_2_q, register_3_q, undriven;

  Clock clock_1 (.out(CLK));
  Pull_Resistor pull_resistor_1 (.node(RES));
  Register register_1 (.D(DATA), .en(AI), .clk(CLK), .Q(register_1_q), .clr(RES));
  Register register_2 (.D(DATA), .en(BI), .clk(CLK), .Q(register_2_q), .clr(RES));
  Register register_3 (.D(DATA), .en(CI), .clk(CLK), .Q(register_3_q), .clr(RES));
  assign DATA = AO ? register_1_q : 8'bz;  // Controlled_Buffer controlled_buffer_1
  assign DATA = BO ? register_2_q : 8'bz;  // Controlled_Buffer controlled_buffer_2
  assign DATA = CO ? register_3_q : 8'bz;  // Controlled_Buffer controlled_buffer_3
  // DipSwitch dipswitch_1: pin names not known
  // DipSwitch #(.number(2)) dipswitch_2: pin names not known; wires that end beside it: dipswitch_2_p1, MAN
  assign CIN = MAN ? undriven_2 : 4'bz;  // Controlled_Buffer controlled_buffer_4
  // DipSwitch #(.number(4)) dipswitch_3: pin names not known
  assign COUT = MAN ? undriven_3 : 4'bz;  // Controlled_Buffer controlled_buffer_5
  // DipSwitch #(.number(4)) dipswitch_4: pin names not known; wires that end beside it: MAN
  assign DATA = dipswitch_2_p1 ? undriven : 8'bz;  // Controlled_Buffer controlled_buffer_6
  Pull_Resistor pull_resistor_2 (.node(CIN));
  Pull_Resistor pull_resistor_3 (.node(COUT));
  Demultiplexer #(.select(4)) demultiplexer_1 (
    .out1(AI), .out2(BI), .out3(CI), .out4(demultiplexer_1_out4), .out5(demultiplexer_1_out5),
    .out6(demultiplexer_1_out6), .out7(demultiplexer_1_out7), .out8(demultiplexer_1_out8),
    .out9(demultiplexer_1_out9), .out10(demultiplexer_1_out10), .out11(demultiplexer_1_out11),
    .out12(demultiplexer_1_out12), .out13(demultiplexer_1_out13), .out14(demultiplexer_1_out14),
    .out15(demultiplexer_1_out15), .in(1'b1), .sel(CIN));  // open: out0
  Demultiplexer #(.select(4)) demultiplexer_2 (
    .out1(AO), .out2(BO), .out3(CO), .out4(demultiplexer_2_out4), .out5(demultiplexer_2_out5),
    .out6(demultiplexer_2_out6), .out7(demultiplexer_2_out7), .out8(demultiplexer_2_out8),
    .out9(demultiplexer_2_out9), .out10(demultiplexer_2_out10), .out11(demultiplexer_2_out11),
    .out12(demultiplexer_2_out12), .out13(demultiplexer_2_out13), .out14(demultiplexer_2_out14),
    .out15(demultiplexer_2_out15), .in(1'b1), .sel(COUT));  // open: out0

  // Notes on the sheet:
  //   Registers
  //   Manual Control
  //   Control
endmodule
